// Logisim project ProjetoCircuitos (com RGB).circ as structural Verilog: 9 circuits, main circuit main
module main (
  input  Confirmar,
  input  [3:0] Chute
);

  wire adivinhe_1_out_4, decoder_1_a_2, decoder_1_b2, decoder_1_bc, decoder_1_c2, decoder_1_d_2, decoder_1_e,
       decoder_1_f, decoder_1_g, Reset_out;

  Button Reset (.out(Reset_out));
  // RGBLed #(.multibit("true")) rgbled_1: pin names not known
  LED Acertou (.in(adivinhe_1_out_4));
  Adivinhe adivinhe_1 (
    .Confirmar(Confirmar), .Chute(Chute), .out_4(adivinhe_1_out_4), .in_2(Reset_out));  // open: out_5, out_6
  Decoder decoder_1 (
    .b2(decoder_1_b2), .a_2(decoder_1_a_2), .f(decoder_1_f), .e(decoder_1_e), .g(decoder_1_g),
    .c2(decoder_1_c2), .d_2(decoder_1_d_2), .bc(decoder_1_bc), .A(Chute[3]), .B(Chute[2]), .C(Chute[1]),
    .D(Chute[0]));
  _7_Segment_Display u_7_segment_display_1 (
    .g(decoder_1_g), .f(decoder_1_f), .a(decoder_1_a_2), .b(decoder_1_b2), .e(decoder_1_e),
    .d(decoder_1_d_2), .c(decoder_1_c2));  // open: dp
  _7_Segment_Display u_7_segment_display_2 (.b(decoder_1_bc), .c(decoder_1_bc));  // open: g, f, a, e, d, dp
endmodule

module Decoder (
  input  A,
  input  B,
  input  C,
  input  D,
  output b2,
  output a_2,
  output f,
  output e,
  output g,
  output c2,
  output d_2,
  output bc
);

  wire and_1_out, and_2_out, and_3_out, and_4_out, and_5_out, and_6_out, and_7_out, and_8_out, and_9_out,
       and_10_out, and_11_out, and_12_out, and_13_out, and_14_out, and_15_out, and_16_out, and_17_out,
       and_18_out, and_19_out, and_20_out, and_21_out, and_22_out, and_23_out, and_24_out, and_25_out,
       and_26_out, and_27_out, and_28_out, and_29_out, and_30_out, and_31_out, and_32_out, and_33_out,
       and_34_out, and_35_out, and_36_out, and_37_out, and_38_out, and_39_out, and_40_out, and_41_out,
       and_42_out, and_43_out, or_1_out, or_2_out, or_3_out, or_4_out, or_5_out, or_7_out, or_8_out,
       or_10_out, or_11_out, or_12_out, or_13_out, or_14_out, or_15_out, or_16_out, or_19_out, or_21_out;

  and and_1 (and_1_out, C, D);
  and and_2 (and_2_out, A, ~C);  // AND_Gate
  and and_3 (and_3_out, A, ~D);  // AND_Gate
  and and_4 (and_4_out, ~C, ~D);  // AND_Gate
  and and_5 (and_5_out, ~A, C);  // AND_Gate
  and and_6 (and_6_out, A, ~C);  // AND_Gate
  and and_7 (and_7_out, ~B, ~D);  // AND_Gate
  and and_8 (and_8_out, B, D);
  and and_9 (and_9_out, ~A, ~C, ~D);  // AND_Gate
  and and_10 (and_10_out, ~A, B, ~C);  // AND_Gate
  and and_11 (and_11_out, A, ~B, ~C);  // AND_Gate
  and and_12 (and_12_out, A, B, C);
  and and_13 (and_13_out, B, C, ~D);  // AND_Gate
  and and_14 (and_14_out, A, C, ~D);  // AND_Gate
  and and_15 (and_15_out, C, ~D);  // AND_Gate
  and and_16 (and_16_out, ~C, ~D);  // AND_Gate
  and and_17 (and_17_out, ~B, C);  // AND_Gate
  and and_18 (and_18_out, A, B);
  and and_19 (and_19_out, A, ~C);  // AND_Gate
  and and_20 (and_20_out, B, ~C);  // AND_Gate
  and and_21 (and_21_out, B, ~D);  // AND_Gate
  and and_22 (and_22_out, ~A, ~C);  // AND_Gate
  and and_23 (and_23_out, A, C);
  and and_24 (and_24_out, ~B, ~C);  // AND_Gate
  and and_25 (and_25_out, B, C);
  and and_26 (and_26_out, ~B, C);  // AND_Gate
  and and_27 (and_27_out, C, ~D);  // AND_Gate
  and and_28 (and_28_out, B, D);
  and and_29 (and_29_out, ~C, ~D);  // AND_Gate
  and and_30 (and_30_out, ~B, ~D);  // AND_Gate
  and and_31 (and_31_out, ~C, D);  // AND_Gate
  and and_32 (and_32_out, A, B);
  and and_33 (and_33_out, A, C);
  and and_34 (and_34_out, ~A, and_1_out);  // AND_Gate
  or or_1 (or_1_out, and_5_out, and_6_out);
  or or_2 (or_2_out, and_7_out, and_8_out);
  and and_35 (and_35_out, ~A, and_15_out);  // AND_Gate
  and and_36 (and_36_out, A, and_16_out);
  and and_37 (and_37_out, ~B, ~D);  // AND_Gate
  and and_38 (and_38_out, ~A, and_17_out);  // AND_Gate
  or or_3 (or_3_out, and_19_out, and_20_out);
  or or_4 (or_4_out, and_22_out, and_23_out);
  or or_5 (or_5_out, and_24_out, and_25_out);
  and and_39 (and_39_out, ~A, and_26_out);  // AND_Gate
  and and_40 (and_40_out, ~A, and_27_out);  // AND_Gate
  and and_41 (and_41_out, A, and_28_out);
  and and_42 (and_42_out, A, and_29_out);
  and and_43 (and_43_out, B, and_31_out);
  or or_6 (bc, and_32_out, and_33_out);
  or or_7 (or_7_out, and_34_out, and_2_out);
  or or_8 (or_8_out, and_3_out, ~B);  // OR_Gate
  or or_9 (a_2, or_1_out, or_2_out);
  or or_10 (or_10_out, and_36_out, and_37_out);
  or or_11 (or_11_out, and_38_out, and_18_out);
  or or_12 (or_12_out, or_4_out, or_5_out);
  or or_13 (or_13_out, and_39_out, and_40_out);
  or or_14 (or_14_out, and_41_out, and_42_out);
  or or_15 (or_15_out, and_30_out, and_43_out);
  or or_16 (or_16_out, or_7_out, or_8_out);
  or or_17 (f, and_9_out, and_10_out, and_11_out, and_12_out, and_13_out, and_14_out);
  or or_18 (e, and_35_out, or_10_out);
  or or_19 (or_19_out, or_11_out, or_3_out);
  or or_20 (c2, or_12_out, D);
  or or_21 (or_21_out, or_13_out, or_14_out);
  or or_22 (b2, or_16_out, and_4_out);
  or or_23 (g, or_19_out, and_21_out);
  or or_24 (d_2, or_21_out, or_15_out);
endmodule

module Adivinhe (
  input  Confirmar,
  input  in_2,
  input  [3:0] Chute,
  output out_4,
  output [7:0] out_5,
  output [7:0] out_6
);

  wire comparador_1_out_3;
  wire [3:0] \diferença , not_1_out, random_1_out;

  Random #(.width(4)) random_1 (.clk(in_2), .out(random_1_out));  // open: next, clr
  assign not_1_out = ~\diferença ;  // NOT_Gate not_1, 4 bits wide
  assign out_5[7:4] = not_1_out & {4{Confirmar}};  // AND_Gate and_1, 4 bits wide
  \Diferença  \diferença_1  (.\Diferença (\diferença ), .Chute_A(Chute), .\Aleatório_B (random_1_out));
  Comparador comparador_1 (.out_3(comparador_1_out_3), .Chute(Chute), .\Valor__Aleatório (random_1_out));
  assign out_6[7:4] = {4{Confirmar}} & \diferença ;  // AND_Gate and_2, 4 bits wide
  and and_3 (out_4, Confirmar, comparador_1_out_3);

  assign out_5[3:0] = 4'b0000;
  assign out_6[3:0] = 4'b0000;
endmodule

module \Diferença  (
  input  [3:0] Chute_A,
  input  [3:0] \Aleatório_B ,
  output [3:0] \Diferença 
);

  wire [3:0] verifica_a_b_1_chute, verifica_a_b_1_numeromisterioso;

  Verifica_A_B verifica_a_b_1 (
    .A(Chute_A), .B(\Aleatório_B ), .Chute(verifica_a_b_1_chute),
    .NumeroMisterioso(verifica_a_b_1_numeromisterioso));
  Subtrator subtrator_1 (
    .Valor_1(verifica_a_b_1_chute), .Valor_2(verifica_a_b_1_numeromisterioso), ._3(\Diferença [3]),
    ._2(\Diferença [2]), ._1(\Diferença [1]), ._0(\Diferença [0]));
endmodule

module SubCompleto (
  input  A,
  input  B,
  input  Carry_in,
  output \Diferença ,
  output B_out
);

  wire and_1_out, and_2_out, and_3_out, xor_1_out;

  xor xor_1 (xor_1_out, B, A);
  and and_1 (and_1_out, ~A, Carry_in);  // AND_Gate
  and and_2 (and_2_out, ~A, B);  // AND_Gate
  and and_3 (and_3_out, B, Carry_in);
  xor xor_2 (\Diferença , xor_1_out, Carry_in);
  or or_1 (B_out, and_1_out, and_2_out, and_3_out);
endmodule

module Verifica_A_B (
  input  [3:0] A,
  input  [3:0] B,
  output [3:0] Chute,
  output [3:0] NumeroMisterioso
);

  wire a_b, and_1_out, and_2_out, and_3_out, and_4_out, not_1_out, not_2_out, not_3_out, not_4_out,
       not_5_out, not_6_out, not_7_out, not_8_out, xnor_1_out, xnor_2_out, xnor_3_out, xnor_4_out,
       xnor_5_out, xnor_6_out;

  Multiplexador multiplexador_1 (.out_4(Chute[3]), .E0(A[3]), .E1(not_1_out), .Selecao(a_b));
  not not_1 (not_1_out, A[3]);
  Multiplexador multiplexador_2 (.out_4(Chute[2]), .E0(A[2]), .E1(not_2_out), .Selecao(a_b));
  not not_2 (not_2_out, A[2]);
  Multiplexador multiplexador_3 (.out_4(Chute[1]), .E0(A[1]), .E1(not_3_out), .Selecao(a_b));
  not not_3 (not_3_out, A[1]);
  Multiplexador multiplexador_4 (.out_4(Chute[0]), .E0(A[0]), .E1(not_4_out), .Selecao(a_b));
  not not_4 (not_4_out, A[0]);
  Multiplexador multiplexador_5 (.out_4(NumeroMisterioso[3]), .E0(B[3]), .E1(not_5_out), .Selecao(a_b));
  not not_5 (not_5_out, B[3]);
  Multiplexador multiplexador_6 (.out_4(NumeroMisterioso[2]), .E0(B[2]), .E1(not_6_out), .Selecao(a_b));
  not not_6 (not_6_out, B[2]);
  Multiplexador multiplexador_7 (.out_4(NumeroMisterioso[1]), .E0(B[1]), .E1(not_7_out), .Selecao(a_b));
  not not_7 (not_7_out, B[1]);
  Multiplexador multiplexador_8 (.out_4(NumeroMisterioso[0]), .E0(B[0]), .E1(not_8_out), .Selecao(a_b));
  not not_8 (not_8_out, B[0]);
  and and_1 (and_1_out, ~A[3], B[3]);  // AND_Gate
  xnor xnor_1 (xnor_1_out, A[3], B[3]);
  xnor xnor_2 (xnor_2_out, A[3], B[3]);
  xnor xnor_3 (xnor_3_out, A[2], B[2]);
  xnor xnor_4 (xnor_4_out, A[3], B[3]);
  xnor xnor_5 (xnor_5_out, A[2], B[2]);
  xnor xnor_6 (xnor_6_out, A[1], B[1]);
  and and_2 (and_2_out, xnor_1_out, ~A[2], B[2]);  // AND_Gate
  and and_3 (and_3_out, xnor_2_out, xnor_3_out, ~A[1], B[1]);  // AND_Gate
  and and_4 (and_4_out, xnor_4_out, xnor_5_out, xnor_6_out, ~A[0], B[0]);  // AND_Gate
  or or_1 (a_b, and_1_out, and_2_out, and_3_out, and_4_out);
endmodule

module Multiplexador (
  input  E0,
  input  E1,
  input  Selecao,
  output out_4
);

  wire and_1_out, and_2_out;

  and and_1 (and_1_out, E0, ~Selecao);  // AND_Gate
  and and_2 (and_2_out, E1, Selecao);
  or or_1 (out_4, and_1_out, and_2_out);
endmodule

module Subtrator (
  input  [3:0] Valor_1,
  input  [3:0] Valor_2,
  output _3,
  output _2,
  output _1,
  output _0
);

  wire subcompleto_2_b_out, subcompleto_3_b_out, subcompleto_4_b_out;

  SubCompleto subcompleto_1 (
    .A(Valor_1[3]), .B(Valor_2[3]), .Carry_in(subcompleto_2_b_out), .\Diferença (_3));  // open: B_out
  SubCompleto subcompleto_2 (
    .A(Valor_1[2]), .B(Valor_2[2]), .Carry_in(subcompleto_3_b_out), .B_out(subcompleto_2_b_out),
    .\Diferença (_2));
  SubCompleto subcompleto_3 (
    .A(Valor_1[1]), .B(Valor_2[1]), .Carry_in(subcompleto_4_b_out), .B_out(subcompleto_3_b_out),
    .\Diferença (_1));
  SubCompleto subcompleto_4 (
    .A(Valor_1[0]), .B(Valor_2[0]), .Carry_in(1'b0), .B_out(subcompleto_4_b_out), .\Diferença (_0));

  // Other names for the same wires on the sheet: a1 = Valor_1[0]; a2 = Valor_1[1]; a3 = Valor_1[2]; a4 = Valor_1[3];
  //   b1 = Valor_2[0]; b2 = Valor_2[1]; b3 = Valor_2[2]; b4 = Valor_2[3]
endmodule

module Comparador (
  input  [3:0] Chute,
  input  [3:0] \Valor__Aleatório ,
  output out_3
);

  wire xnor_1_out, xnor_2_out, xnor_3_out, xnor_4_out;

  xnor xnor_1 (xnor_1_out, Chute[3], \Valor__Aleatório [3]);
  xnor xnor_2 (xnor_2_out, Chute[2], \Valor__Aleatório [2]);
  xnor xnor_3 (xnor_3_out, Chute[1], \Valor__Aleatório [1]);
  xnor xnor_4 (xnor_4_out, Chute[0], \Valor__Aleatório [0]);
  and and_1 (out_3, xnor_1_out, xnor_2_out, xnor_3_out, xnor_4_out);
endmodule
